// Logisim project BCDADDER.circ as structural Verilog: 1 circuit, main circuit main
module main (
  input  [3:0] in_1,
  input  in_2,
  input  in_3,
  input  [3:0] in_4,
  input  [7:0] in_5,
  input  [7:0] in_6,
  input  in_7,
  input  [3:0] in_8,
  input  [3:0] in_9,
  input  [3:0] in_10,
  input  [3:0] in_11,
  output [3:0] out_12,
  output [7:0] out_13,
  output out_14,
  output [3:0] out_15
);

  wire adder_1_cout, adder_2_cout, adder_4_cout, and_1_out, and_2_out, clock_1_out, clock_2_out,
       comparator_1_gt, comparator_2_gt, or_1_out, or_2_out;
  wire [3:0] adder_1_out, adder_2_out, adder_3_out, multiplexer_1_out, multiplexer_1_out_2, register_1_q,
       register_2_q, subtractor_1_out, subtractor_2_out;

  Multiplexer #(.width(8)) multiplexer_1 (
    .in0(in_5), .in1({subtractor_1_out, adder_3_out}), .out({multiplexer_1_out_2, multiplexer_1_out}),
    .sel(in_3));
  Adder #(.width(4)) adder_1 (
    .a(multiplexer_1_out), .b(in_6[3:0]), .out(adder_1_out), .cout(adder_1_cout));  // open: cin
  Comparator #(.width(4)) comparator_1 (.a(adder_1_out), .b(in_4), .gt(comparator_1_gt));  // open: eq, lt
  Adder #(.width(4)) adder_2 (
    .a(multiplexer_1_out_2), .b(in_6[7:4]), .out(adder_2_out), .cin(adder_1_cout), .cout(adder_2_cout));
  Subtractor #(.width(4)) subtractor_1 (.a(in_5[7:4]), .b(in_10), .out(subtractor_1_out));  // open: bin, bout
  Subtractor #(.width(4)) subtractor_2 (.a(in_5[3:0]), .b(in_10), .out(subtractor_2_out));  // open: bin, bout
  or or_1 (or_1_out, comparator_1_gt, adder_1_cout);
  Comparator #(.width(4)) comparator_2 (.a(adder_2_out), .b(in_9), .gt(comparator_2_gt));  // open: eq, lt
  and and_1 (and_1_out, or_1_out, in_2);
  Register #(.width(4)) register_1 (.D(in_1), .en(or_1_out), .Q(register_1_q), .clk(clock_1_out), .clr(and_1_out));
  Clock clock_1 (.out(clock_1_out));
  and and_2 (and_2_out, or_2_out, in_7);
  Register #(.width(4)) register_2 (.D(in_8), .en(or_2_out), .Q(register_2_q), .clk(clock_2_out), .clr(and_2_out));
  Clock clock_2 (.out(clock_2_out));
  or or_2 (or_2_out, comparator_2_gt, adder_2_cout);
  Adder #(.width(4)) adder_3 (.a(subtractor_2_out), .b(in_11), .out(adder_3_out));  // open: cin, cout
  Adder #(.width(4)) adder_4 (.a(register_1_q), .b(adder_1_out), .out(out_12), .cout(adder_4_cout));  // open: cin
  Adder #(.width(4)) adder_5 (.a(register_2_q), .b(adder_2_out), .out(out_13[7:4]), .cin(adder_4_cout), .cout(out_14));

  assign out_13[3:0] = out_12;
  assign out_15 = out_13[7:4];
endmodule
