// Logisim project BCDADDERBUFF.circ as structural Verilog: 1 circuit, main circuit main
module main (
  input  [3:0] in_1,
  input  [3:0] in_2,
  input  [7:0] in_3,
  input  [7:0] in_4,
  input  [3:0] in_5,
  input  [3:0] in_6,
  input  [3:0] in_7,
  input  [3:0] in_8,
  output [3:0] out_9,
  output [3:0] out_10,
  output out_11,
  output out_12
);

  wire adder_1_cout, adder_3_cout, comparator_1_gt, comparator_2_gt;
  wire [3:0] adder_1_out, adder_2_out, controlled_buffer_1_out, controlled_buffer_2_out;

  Adder #(.width(4)) adder_1 (.a(in_3[3:0]), .b(in_4[3:0]), .out(adder_1_out), .cout(adder_1_cout));  // open: cin
  Adder #(.width(4)) adder_2 (.a(in_3[7:4]), .b(in_4[7:4]), .out(adder_2_out), .cin(adder_1_cout));  // open: cout
  Comparator #(.width(4)) comparator_1 (.a(adder_1_out), .b(in_2), .gt(comparator_1_gt));  // open: eq, lt
  Comparator #(.width(4)) comparator_2 (.a(adder_2_out), .b(in_6), .gt(comparator_2_gt));  // open: eq, lt
  assign controlled_buffer_1_out = comparator_1_gt ? in_1 : 4'bz;  // Controlled_Buffer controlled_buffer_1
  assign controlled_buffer_2_out = comparator_2_gt ? in_5 : 4'bz;  // Controlled_Buffer controlled_buffer_2
  Comparator #(.width(4)) comparator_3 (.a(in_7), .b(in_8), .gt(out_12));  // open: eq, lt
  Adder #(.width(4)) adder_3 (
    .a(controlled_buffer_1_out), .b(adder_1_out), .out(out_9), .cout(adder_3_cout));  // open: cin
  Adder #(.width(4)) adder_4 (
    .a(controlled_buffer_2_out), .b(adder_2_out), .out(out_10), .cin(adder_3_cout), .cout(out_11));
endmodule
