// Logisim project COMMON BUS-1.circ as structural Verilog: 1 circuit, main circuit main
module main (
  input  [1:0] in_1,
  input  [1:0] in_2,
  input  [1:0] in_3,
  input  [1:0] in_4,
  input  d1,
  input  d0,
  input  in_7,
  input  in_8,
  input  c1,
  input  c3,
  input  c2,
  input  in_12,
  input  b1,
  input  in_14,
  input  c1_2,
  input  in_16,
  input  a1,
  input  in_18,
  input  c0,
  input  in_20,
  output out_21,
  output out_22,
  output out_23,
  output out_24
);

  wire clock_1_out, clock_2_out, clock_3_out, clock_4_out, d_ff_1_q, d_ff_2_q, d_ff_3_q, d_ff_4_q, d_ff_5_q,
       d_ff_6_q, d_ff_7_q, d_ff_8_q, d_ff_9_q, d_ff_10_q, d_ff_11_q, d_ff_12_q, d_ff_13_q, d_ff_14_q,
       d_ff_15_q, d_ff_16_q;

  Clock clock_1 (.out(clock_1_out));
  Multiplexer #(.select(2)) multiplexer_1 (
    .in0(d_ff_1_q), .in1(d_ff_2_q), .in2(d_ff_3_q), .in3(d_ff_4_q), .out(out_21), .sel(in_1));
  D_Flip_Flop d_ff_1 (.clk(clock_1_out), .D(in_7), .Q(d_ff_1_q));  // open: Qn, preset, en, reset
  D_Flip_Flop d_ff_2 (.clk(clock_1_out), .D(c3), .Q(d_ff_2_q));  // open: Qn, preset, en, reset
  D_Flip_Flop d_ff_3 (.clk(clock_1_out), .D(in_14), .Q(d_ff_3_q));  // open: Qn, preset, en, reset
  D_Flip_Flop d_ff_4 (.clk(clock_1_out), .D(in_18), .Q(d_ff_4_q));  // open: Qn, preset, en, reset
  Multiplexer #(.select(2)) multiplexer_2 (
    .in0(d_ff_5_q), .in1(d_ff_6_q), .in2(d_ff_7_q), .in3(d_ff_8_q), .out(out_22), .sel(in_2));
  Clock clock_2 (.out(clock_2_out));
  D_Flip_Flop d_ff_5 (.clk(clock_2_out), .D(in_8), .Q(d_ff_5_q));  // open: Qn, preset, en, reset
  D_Flip_Flop d_ff_6 (.clk(clock_2_out), .D(c2), .Q(d_ff_6_q));  // open: Qn, preset, en, reset
  D_Flip_Flop d_ff_7 (.clk(clock_2_out), .D(c1_2), .Q(d_ff_7_q));  // open: Qn, preset, en, reset
  Multiplexer #(.select(2)) multiplexer_3 (
    .in0(d_ff_9_q), .in1(d_ff_10_q), .in2(d_ff_11_q), .in3(d_ff_12_q), .out(out_23), .sel(in_3));
  Clock clock_3 (.out(clock_3_out));
  D_Flip_Flop d_ff_8 (.clk(clock_2_out), .D(c0), .Q(d_ff_8_q));  // open: Qn, preset, en, reset
  D_Flip_Flop d_ff_9 (.clk(clock_3_out), .D(d1), .Q(d_ff_9_q));  // open: Qn, preset, en, reset
  D_Flip_Flop d_ff_10 (.clk(clock_3_out), .D(c1), .Q(d_ff_10_q));  // open: Qn, preset, en, reset
  D_Flip_Flop d_ff_11 (.clk(clock_3_out), .D(b1), .Q(d_ff_11_q));  // open: Qn, preset, en, reset
  D_Flip_Flop d_ff_12 (.clk(clock_3_out), .D(a1), .Q(d_ff_12_q));  // open: Qn, preset, en, reset
  Multiplexer #(.select(2)) multiplexer_4 (
    .in0(d_ff_13_q), .in1(d_ff_14_q), .in2(d_ff_15_q), .in3(d_ff_16_q), .out(out_24), .sel(in_4));
  Clock clock_4 (.out(clock_4_out));
  D_Flip_Flop d_ff_13 (.clk(clock_4_out), .D(d0), .Q(d_ff_13_q));  // open: Qn, preset, en, reset
  D_Flip_Flop d_ff_14 (.clk(clock_4_out), .D(in_12), .Q(d_ff_14_q));  // open: Qn, preset, en, reset
  D_Flip_Flop d_ff_15 (.clk(clock_4_out), .D(in_16), .Q(d_ff_15_q));  // open: Qn, preset, en, reset
  D_Flip_Flop d_ff_16 (.clk(clock_4_out), .D(in_20), .Q(d_ff_16_q));  // open: Qn, preset, en, reset

  // Notes on the sheet:
  //   d3
  //   b3
  //   a3
  //   d2
  //   c2
  //   b2
  //   a1
  //   a3
  //   c0
  //   b0
  //   a0
endmodule
