// Logisim project COMMON BUS-2.circ as structural Verilog: 1 circuit, main circuit main
module main (
  input  D3,
  input  C2,
  input  B3,
  input  A3,
  input  D2,
  input  in_6,
  input  in_7,
  input  in_8,
  input  in_9,
  input  in_10,
  input  in_11,
  input  in_12,
  input  in_13,
  input  in_14,
  input  in_15,
  input  in_16,
  input  [1:0] in_17,
  input  [1:0] in_18,
  input  [1:0] in_19,
  input  [1:0] in_20,
  output out_21,
  output out_22,
  output out_23,
  output out_24,
  output out_25,
  output out_26,
  output out_27,
  output out_28,
  output out_29,
  output out_30,
  output out_31,
  output out_32,
  output out_33,
  output out_34,
  output out_35,
  output out_36
);

  wire decoder_1_out0, decoder_1_out1, decoder_1_out2, decoder_1_out3, decoder_2_out0, decoder_2_out1,
       decoder_2_out2, decoder_2_out3, decoder_3_out0, decoder_3_out1, decoder_3_out2, decoder_3_out3,
       decoder_4_out0, decoder_4_out1, decoder_4_out2, decoder_4_out3;

  assign out_21 = decoder_1_out3 ? D3 : 1'bz;  // Controlled_Buffer controlled_buffer_1
  assign out_25 = decoder_1_out2 ? D2 : 1'bz;  // Controlled_Buffer controlled_buffer_2
  assign out_29 = decoder_1_out1 ? in_9 : 1'bz;  // Controlled_Buffer controlled_buffer_3
  assign out_33 = decoder_1_out0 ? in_13 : 1'bz;  // Controlled_Buffer controlled_buffer_4
  Decoder #(.select(2)) decoder_1 (
    .out0(decoder_1_out0), .out1(decoder_1_out1), .out2(decoder_1_out2), .out3(decoder_1_out3), .sel(in_17));
  assign out_22 = decoder_2_out3 ? C2 : 1'bz;  // Controlled_Buffer controlled_buffer_5
  assign out_26 = decoder_2_out2 ? in_6 : 1'bz;  // Controlled_Buffer controlled_buffer_6
  assign out_30 = decoder_2_out1 ? in_10 : 1'bz;  // Controlled_Buffer controlled_buffer_7
  assign out_34 = decoder_2_out0 ? in_14 : 1'bz;  // Controlled_Buffer controlled_buffer_8
  Decoder #(.select(2)) decoder_2 (
    .out0(decoder_2_out0), .out1(decoder_2_out1), .out2(decoder_2_out2), .out3(decoder_2_out3), .sel(in_18));
  assign out_23 = decoder_3_out3 ? B3 : 1'bz;  // Controlled_Buffer controlled_buffer_9
  assign out_27 = decoder_3_out2 ? in_7 : 1'bz;  // Controlled_Buffer controlled_buffer_10
  assign out_31 = decoder_3_out1 ? in_11 : 1'bz;  // Controlled_Buffer controlled_buffer_11
  assign out_35 = decoder_3_out0 ? in_15 : 1'bz;  // Controlled_Buffer controlled_buffer_12
  Decoder #(.select(2)) decoder_3 (
    .out0(decoder_3_out0), .out1(decoder_3_out1), .out2(decoder_3_out2), .out3(decoder_3_out3), .sel(in_19));
  assign out_24 = decoder_4_out3 ? A3 : 1'bz;  // Controlled_Buffer controlled_buffer_13
  assign out_28 = decoder_4_out2 ? in_8 : 1'bz;  // Controlled_Buffer controlled_buffer_14
  assign out_32 = decoder_4_out1 ? in_12 : 1'bz;  // Controlled_Buffer controlled_buffer_15
  assign out_36 = decoder_4_out0 ? in_16 : 1'bz;  // Controlled_Buffer controlled_buffer_16
  Decoder #(.select(2)) decoder_4 (
    .out0(decoder_4_out0), .out1(decoder_4_out1), .out2(decoder_4_out2), .out3(decoder_4_out3), .sel(in_20));

  // Notes on the sheet:
  //   C3
endmodule
