// Logisim project FLOATING POINT.circ as structural Verilog: 1 circuit, main circuit main
module main (
  input  [7:0] in_1,
  input  [3:0] in_2,
  input  [7:0] in_3,
  input  [3:0] in_4,
  input  in_5,
  input  [3:0] in_6,
  input  [3:0] in_7,
  output [3:0] out_8,
  output [3:0] out_9
);

  wire adder_2_cout, adder_6_cout, adder_8_cout, and_1_out, comparator_1_eq, comparator_1_gt,
       comparator_2_eq, comparator_2_gt, multiplexer_3_out, or_1_out, or_2_out, or_3_out;
  wire [3:0] adder_1_out, adder_2_out, adder_3_out, adder_4_out, adder_5_out, adder_6_out, adder_7_out,
       adder_8_out, adder_9_out, multiplexer_1_out, multiplexer_2_out, multiplexer_4_out, multiplexer_5_out,
       multiplexer_6_out, multiplexer_7_out, not_1_out, not_2_out, not_3_out, not_4_out, not_5_out, not_6_out;

  assign not_1_out = ~in_3[3:0];  // NOT_Gate not_1, 4 bits wide
  Adder #(.width(4)) adder_1 (.a(not_1_out), .b(4'b0000), .out(adder_1_out), .cin(in_5));  // open: cout
  assign not_2_out = ~in_3[7:4];  // NOT_Gate not_2, 4 bits wide
  Multiplexer #(.width(4)) multiplexer_1 (.in0(in_3[3:0]), .in1(adder_1_out), .out(multiplexer_1_out), .sel(in_5));
  or or_1 (or_1_out, adder_2_cout, adder_6_cout);
  Multiplexer #(.width(4)) multiplexer_2 (.in0(in_3[7:4]), .in1(not_2_out), .out(multiplexer_2_out), .sel(in_5));
  Adder #(.width(4)) adder_2 (
    .a(in_1[3:0]), .b(multiplexer_1_out), .out(adder_2_out), .cout(adder_2_cout));  // open: cin
  Multiplexer multiplexer_3 (.in0(or_1_out), .in1(adder_2_cout), .out(multiplexer_3_out), .sel(in_5));
  Adder #(.width(4)) adder_3 (
    .a(in_1[7:4]), .b(multiplexer_2_out), .out(adder_3_out), .cin(multiplexer_3_out));  // open: cout
  assign not_3_out = ~in_2;  // NOT_Gate not_3, 4 bits wide
  Comparator #(.width(4), .mode("unsigned")) comparator_1 (
    .a(adder_2_out), .b(in_4), .gt(comparator_1_gt), .eq(comparator_1_eq));  // open: lt
  assign not_4_out = ~in_6;  // NOT_Gate not_4, 4 bits wide
  and and_1 (and_1_out, adder_8_cout, in_5);
  Multiplexer #(.width(4)) multiplexer_4 (.in0(in_2), .in1(adder_4_out), .out(multiplexer_4_out), .sel(in_5));
  Adder #(.width(4)) adder_4 (.a(not_3_out), .b(4'b0000), .out(adder_4_out), .cin(in_5));  // open: cout
  or or_2 (or_2_out, comparator_1_eq, comparator_1_gt);
  Adder #(.width(4)) adder_5 (.a(not_4_out), .b(4'b0000), .out(adder_5_out), .cin(in_5));  // open: cout
  Comparator #(.width(4), .mode("unsigned")) comparator_2 (
    .a(adder_3_out), .b(in_7), .gt(comparator_2_gt), .eq(comparator_2_eq));  // open: lt
  or or_3 (or_3_out, comparator_2_eq, comparator_2_gt);
  Multiplexer #(.width(4)) multiplexer_5 (
    .in0(4'b0000), .in1(multiplexer_4_out), .out(multiplexer_5_out), .sel(or_2_out));
  Multiplexer #(.width(4)) multiplexer_6 (.in0(in_6), .in1(adder_5_out), .out(multiplexer_6_out), .sel(in_5));
  assign not_5_out = ~adder_6_out;  // NOT_Gate not_5, 4 bits wide
  Adder #(.width(4)) adder_6 (
    .a(adder_2_out), .b(multiplexer_5_out), .out(adder_6_out), .cout(adder_6_cout));  // open: cin
  assign not_6_out = ~adder_8_out;  // NOT_Gate not_6, 4 bits wide
  Adder #(.width(4)) adder_7 (.a(not_6_out), .b(4'b0000), .out(adder_7_out), .cin(and_1_out));  // open: cout
  Adder #(.width(4)) adder_8 (
    .a(adder_3_out), .b(multiplexer_7_out), .out(adder_8_out), .cout(adder_8_cout));  // open: cin
  Multiplexer #(.width(4)) multiplexer_7 (
    .in0(4'b0000), .in1(multiplexer_6_out), .out(multiplexer_7_out), .sel(or_3_out));
  Multiplexer #(.width(4)) multiplexer_8 (.in0(adder_6_out), .in1(adder_9_out), .out(out_9), .sel(and_1_out));
  Adder #(.width(4)) adder_9 (.a(not_5_out), .b(4'b0000), .out(adder_9_out), .cin(and_1_out));  // open: cout
  Multiplexer #(.width(4)) multiplexer_9 (.in0(adder_8_out), .in1(adder_7_out), .out(out_8), .sel(and_1_out));

  // Notes on the sheet:
  //   carry
endmodule
