// Logisim project MULTIPIER.circ as structural Verilog: 1 circuit, main circuit main
module main (
  input  [3:0] in_1,
  input  [1:0] in_2,
  input  [7:0] in_3,
  input  in_4,
  input  in_5,
  input  [2:0] in_6,
  input  [2:0] in_7,
  input  [7:0] b,
  input  in_9,
  output [7:0] out_10
);

  wire clock_1_out, clock_2_out, comparator_1_eq;
  wire [2:0] adder_1_out, adder_2_out, and_1_out;
  wire [3:0] shifter_1_out;
  wire [7:0] adder_3_out, register_1_q, register_2_q, shifter_2_out;

  Register register_1 (.D(adder_3_out), .en(in_5), .Q(register_1_q), .clk(clock_1_out));  // open: clr
  Clock clock_1 (.out(clock_1_out));
  Adder #(.width(3)) adder_1 (.a(adder_2_out), .b(in_7), .out(adder_1_out));  // open: cin, cout
  assign and_1_out = in_6 & adder_1_out;  // AND_Gate and_1, 3 bits wide
  Adder #(.width(3)) adder_2 (.a(in_6), .b(and_1_out), .out(adder_2_out));  // open: cin, cout
  Multiplexer #(.width(8)) multiplexer_1 (.in1(b), .out(out_10), .sel(comparator_1_eq));  // open: in0
  Register register_2 (.D(adder_3_out), .en(in_9), .Q(register_2_q), .clk(clock_2_out));  // open: clr
  Clock clock_2 (.out(clock_2_out));
  Shifter #(.width(4), .shift("lr")) shifter_1 (.in(in_1), .\dist (in_2), .out(shifter_1_out));
  Comparator #(.width(1)) comparator_1 (.a(shifter_1_out[0]), .b(in_4), .eq(comparator_1_eq));  // open: gt, lt
  Shifter shifter_2 (.in(out_10), .\dist (adder_2_out), .out(shifter_2_out));
  Adder adder_3 (.a(shifter_2_out), .b(register_2_q), .out(adder_3_out));  // open: cin, cout
endmodule
