// Logisim project PRAC1.circ as structural Verilog: 1 circuit, main circuit main
module main (
  input  W,
  input  X,
  input  Y,
  output A,
  output B,
  output C,
  output CARRY
);

  wire and_1_out, and_2_out, and_4_out, and_5_out, not_1_out, not_2_out, not_3_out, or_1_out;

  not not_1 (not_1_out, Y);
  not not_2 (not_2_out, X);
  not not_3 (not_3_out, W);
  or or_1 (or_1_out, not_1_out, not_2_out);
  and and_1 (and_1_out, X, not_1_out);
  and and_2 (and_2_out, not_2_out, Y);
  and and_3 (CARRY, Y, X, W);
  and and_4 (and_4_out, X, not_3_out, Y);
  and and_5 (and_5_out, W, or_1_out);
  or or_2 (B, and_1_out, and_2_out);
  not not_4 (C, Y);
  or or_3 (A, and_4_out, and_5_out);
endmodule
