// Logisim project PRAC1B.circ as structural Verilog: 1 circuit, main circuit main
module main (
  input  W,
  input  X,
  input  Y,
  output A,
  output B,
  output C
);

  wire and_2_out, and_3_out, not_1_out, or_1_out;

  not not_1 (not_1_out, X);
  or or_1 (or_1_out, X, Y);
  not not_2 (C, Y);
  and and_1 (A, or_1_out, W);
  and and_2 (and_2_out, W, not_1_out, C);
  and and_3 (and_3_out, X, Y);
  or or_2 (B, and_2_out, and_3_out);
endmodule
