// Logisim project PRAC1C.circ as structural Verilog: 1 circuit, main circuit main
module main (
  input  Y,
  input  X,
  input  W,
  input  N,
  input  M,
  input  L,
  output CARRY,
  output C,
  output B,
  output A
);

  wire adder_1_cout, adder_2_cout;

  Adder #(.width(1)) adder_1 (.a(W), .b(L), .out(A), .cout(adder_1_cout));  // open: cin
  Adder #(.width(1)) adder_2 (.a(X), .b(M), .out(B), .cin(adder_1_cout), .cout(adder_2_cout));
  Adder #(.width(1)) adder_3 (.a(Y), .b(N), .out(C), .cin(adder_2_cout), .cout(CARRY));
endmodule
