// Logisim project PRAC1D.circ as structural Verilog: 1 circuit, main circuit main
module main (
  input  in_1,
  input  in_2,
  input  in_3,
  input  in_4,
  input  in_5,
  input  in_6,
  output out_7,
  output out_8,
  output out_9,
  output out_10
);

  wire adder_1_cout, adder_2_cout, adder_3_cout;

  Adder #(.width(1)) adder_1 (.a(in_3), .b(in_6), .out(out_10), .cout(adder_1_cout));  // open: cin
  Adder #(.width(1)) adder_2 (.a(in_2), .b(in_5), .out(out_9), .cin(adder_1_cout), .cout(adder_2_cout));
  Adder #(.width(1)) adder_3 (.a(in_1), .b(in_4), .out(out_8), .cin(adder_2_cout), .cout(adder_3_cout));
  not not_1 (out_7, adder_3_cout);
endmodule
