// Logisim project PRAC2A.circ as structural Verilog: 1 circuit, main circuit main
module main (
  input  [2:0] in_1,
  input  [2:0] in_2,
  input  [2:0] in_3,
  input  [2:0] in_4,
  input  [2:0] in_5,
  output [2:0] out_6
);

  wire comparator_1_eq, comparator_2_eq, comparator_3_eq;
  wire [2:0] divider_1_rem, divider_2_rem, divider_3_rem, multiplexer_1_out, multiplexer_2_out,
       multiplexer_3_out;

  Divider #(.width(3)) divider_1 (.a(in_1), .b(in_2), .rem(divider_1_rem));  // open: out, upper
  Divider #(.width(3)) divider_2 (.a(in_2), .b(divider_1_rem), .rem(divider_2_rem));  // open: out, upper
  Divider #(.width(3)) divider_3 (.a(divider_1_rem), .b(divider_2_rem), .rem(divider_3_rem));  // open: out, upper
  Comparator #(.width(3)) comparator_1 (.a(in_3), .b(divider_1_rem), .eq(comparator_1_eq));  // open: gt, lt
  Comparator #(.width(3)) comparator_2 (.a(in_4), .b(divider_2_rem), .eq(comparator_2_eq));  // open: gt, lt
  Comparator #(.width(3)) comparator_3 (.a(in_5), .b(divider_3_rem), .eq(comparator_3_eq));  // open: gt, lt
  Multiplexer #(.width(3)) multiplexer_1 (.in0(in_3), .in1(in_2), .out(multiplexer_1_out), .sel(comparator_1_eq));
  Multiplexer #(.width(3)) multiplexer_2 (
    .in0(in_4), .in1(divider_1_rem), .out(multiplexer_2_out), .sel(comparator_2_eq));
  Multiplexer #(.width(3)) multiplexer_3 (
    .in0(in_5), .in1(divider_2_rem), .out(multiplexer_3_out), .sel(comparator_3_eq));
  assign out_6 = multiplexer_1_out | multiplexer_2_out | multiplexer_3_out;  // OR_Gate or_1, 3 bits wide
endmodule
