// Logisim project PRAC2B.circ as structural Verilog: 1 circuit, main circuit main
module main (
  input  in_1,
  input  [2:0] in_2,
  input  in_3,
  input  [2:0] in_4,
  input  [2:0] in_5,
  input  [2:0] in_6,
  output [2:0] out_7
);

  wire and_1_out, clock_1_out, comparator_1_eq, comparator_2_eq, multiplexer_1_out;
  wire [2:0] divider_1_rem, divider_2_rem;

  Counter #(.width(3), .max('h7)) counter_1 (
    .load(in_1), .count(in_1), .Q(out_7), .clk(multiplexer_1_out));  // open: D, carry, clr
  Divider #(.width(3)) divider_1 (.a(in_2), .b(out_7), .rem(divider_1_rem));  // open: out, upper
  Divider #(.width(3)) divider_2 (.a(in_5), .b(out_7), .rem(divider_2_rem));  // open: out, upper
  Comparator #(.width(3)) comparator_1 (.a(in_4), .b(divider_1_rem), .eq(comparator_1_eq));  // open: gt, lt
  Comparator #(.width(3)) comparator_2 (.a(in_6), .b(divider_2_rem), .eq(comparator_2_eq));  // open: gt, lt
  Clock clock_1 (.out(clock_1_out));
  and and_1 (and_1_out, comparator_1_eq, comparator_2_eq);
  Multiplexer multiplexer_1 (.in0(clock_1_out), .in1(in_3), .out(multiplexer_1_out), .sel(and_1_out));
endmodule
