// Logisim project additional  arith.circ as structural Verilog: 1 circuit, main circuit main
module main (
  input  in_1,
  input  [1:0] in_2,
  input  [3:0] in_3,
  input  in_4,
  input  [3:0] in_5,
  output [3:0] out_6
);

  wire adder_1_cout, adder_2_cout, adder_3_cout, multiplexer_1_out, multiplexer_2_out, multiplexer_3_out,
       multiplexer_4_out, not_1_out, not_2_out, not_3_out, not_4_out, not_5_out, not_6_out, not_7_out,
       not_8_out;

  not not_1 (not_1_out, in_3[0]);
  Multiplexer #(.select(2)) multiplexer_1 (
    .in0(in_3[0]), .in1(not_1_out), .in2(in_1), .in3(not_2_out), .out(multiplexer_1_out), .sel(in_2));
  not not_2 (not_2_out, in_1);
  not not_3 (not_3_out, in_3[1]);
  Multiplexer #(.select(2)) multiplexer_2 (
    .in0(in_3[1]), .in1(not_3_out), .in2(in_1), .in3(not_4_out), .out(multiplexer_2_out), .sel(in_2));
  not not_4 (not_4_out, in_1);
  not not_5 (not_5_out, in_3[2]);
  Multiplexer #(.select(2)) multiplexer_3 (
    .in0(in_3[2]), .in1(not_5_out), .in2(in_1), .in3(not_6_out), .out(multiplexer_3_out), .sel(in_2));
  not not_6 (not_6_out, in_1);
  not not_7 (not_7_out, in_3[3]);
  Multiplexer #(.select(2)) multiplexer_4 (
    .in0(in_3[3]), .in1(not_7_out), .in2(in_1), .in3(not_8_out), .out(multiplexer_4_out), .sel(in_2));
  not not_8 (not_8_out, in_1);
  Adder #(.width(1)) adder_1 (.a(multiplexer_1_out), .b(in_5[0]), .out(out_6[0]), .cin(in_4), .cout(adder_1_cout));
  Adder #(.width(1)) adder_2 (
    .a(multiplexer_2_out), .b(in_5[1]), .out(out_6[1]), .cin(adder_1_cout), .cout(adder_2_cout));
  Adder #(.width(1)) adder_3 (
    .a(multiplexer_3_out), .b(in_5[2]), .out(out_6[2]), .cin(adder_2_cout), .cout(adder_3_cout));
  Adder #(.width(1)) adder_4 (.a(multiplexer_4_out), .b(in_5[3]), .out(out_6[3]), .cin(adder_3_cout));  // open: cout
endmodule
