// Logisim project arinlog.circ as structural Verilog: 1 circuit, main circuit main
module main (
  input  [3:0] A,
  input  [3:0] B,
  input  in_3,
  input  in_4,
  input  in_5,
  output out_6,
  output [3:0] out_7
);

  wire [3:0] adder_1_out, and_1_out, multiplexer_1_out, multiplexer_2_out, not_1_out, not_2_out, or_1_out,
       xor_1_out;

  assign not_1_out = ~A;  // NOT_Gate not_1, 4 bits wide
  assign xor_1_out = A ^ B;  // XOR_Gate xor_1, 4 bits wide
  assign not_2_out = ~B;  // NOT_Gate not_2, 4 bits wide
  assign or_1_out = A | B;  // OR_Gate or_1, 4 bits wide
  assign and_1_out = A & B;  // AND_Gate and_1, 4 bits wide
  Multiplexer #(.select(2), .width(4)) multiplexer_1 (
    .in0(B), .in1(4'b0000), .in2(4'b1111), .in3(not_2_out), .out(multiplexer_1_out), .sel({in_4, in_5}));
  Multiplexer #(.select(2), .width(4)) multiplexer_2 (
    .in0(and_1_out), .in1(or_1_out), .in2(xor_1_out), .in3(not_1_out), .out(multiplexer_2_out),
    .sel({in_4, in_5}));
  Adder #(.width(4)) adder_1 (.a(A), .b(multiplexer_1_out), .out(adder_1_out), .cin(in_5), .cout(out_6));
  Multiplexer #(.width(4)) multiplexer_3 (.in0(adder_1_out), .in1(multiplexer_2_out), .out(out_7), .sel(in_3));

  // Notes on the sheet:
  //   s2
  //   s1
  //   cin
endmodule
