// Logisim project prac5.circ as structural Verilog: 1 circuit, main circuit main
module main (
  input  in_1,
  input  [1:0] in_2,
  input  [3:0] in_3,
  input  in_4,
  input  [3:0] in_5,
  input  in_6,
  output [3:0] out_7
);

  wire adder_1_cout, adder_2_cout, adder_3_cout, multiplexer_1_out, multiplexer_2_out, multiplexer_3_out,
       multiplexer_4_out, not_2_out, not_3_out, not_4_out, not_5_out, not_6_out, not_7_out, not_8_out,
       not_9_out;
  wire [3:0] adder_1_out, and_1_out, multiplexer_5_out, not_1_out, or_1_out, xor_1_out;

  assign not_1_out = ~in_3;  // NOT_Gate not_1, 4 bits wide
  assign and_1_out = in_3 & in_5;  // AND_Gate and_1, 4 bits wide
  assign or_1_out = in_3 | in_5;  // OR_Gate or_1, 4 bits wide
  assign xor_1_out = in_3 ^ in_5;  // XOR_Gate xor_1, 4 bits wide
  not not_2 (not_2_out, in_3[0]);
  Multiplexer #(.select(2)) multiplexer_1 (
    .in0(in_3[0]), .in1(not_2_out), .in2(in_1), .in3(not_3_out), .out(multiplexer_1_out), .sel(in_2));
  not not_3 (not_3_out, in_1);
  not not_4 (not_4_out, in_3[1]);
  Multiplexer #(.select(2)) multiplexer_2 (
    .in0(in_3[1]), .in1(not_4_out), .in2(in_1), .in3(not_5_out), .out(multiplexer_2_out), .sel(in_2));
  not not_5 (not_5_out, in_1);
  not not_6 (not_6_out, in_3[2]);
  Multiplexer #(.select(2)) multiplexer_3 (
    .in0(in_3[2]), .in1(not_6_out), .in2(in_1), .in3(not_7_out), .out(multiplexer_3_out), .sel(in_2));
  not not_7 (not_7_out, in_1);
  not not_8 (not_8_out, in_3[3]);
  Multiplexer #(.select(2)) multiplexer_4 (
    .in0(in_3[3]), .in1(not_8_out), .in2(in_1), .in3(not_9_out), .out(multiplexer_4_out), .sel(in_2));
  not not_9 (not_9_out, in_1);
  Multiplexer #(.select(2)) multiplexer_5 (
    .in0(and_1_out[0]), .in1(or_1_out[0]), .in2(not_1_out[0]), .in3(xor_1_out[0]),
    .out(multiplexer_5_out[0]), .sel(in_2));
  Multiplexer #(.select(2)) multiplexer_6 (
    .in0(and_1_out[1]), .in1(or_1_out[1]), .in2(not_1_out[1]), .in3(xor_1_out[1]),
    .out(multiplexer_5_out[1]), .sel(in_2));
  Multiplexer #(.select(2)) multiplexer_7 (
    .in0(and_1_out[2]), .in1(or_1_out[2]), .in2(not_1_out[2]), .in3(xor_1_out[2]),
    .out(multiplexer_5_out[2]), .sel(in_2));
  Multiplexer #(.select(2)) multiplexer_8 (
    .in0(and_1_out[3]), .in1(or_1_out[3]), .in2(not_1_out[3]), .in3(xor_1_out[3]),
    .out(multiplexer_5_out[3]), .sel(in_2));
  Adder #(.width(1)) adder_1 (
    .a(multiplexer_1_out), .b(in_5[0]), .out(adder_1_out[0]), .cin(in_4), .cout(adder_1_cout));
  Adder #(.width(1)) adder_2 (
    .a(multiplexer_2_out), .b(in_5[1]), .out(adder_1_out[1]), .cin(adder_1_cout), .cout(adder_2_cout));
  Adder #(.width(1)) adder_3 (
    .a(multiplexer_3_out), .b(in_5[2]), .out(adder_1_out[2]), .cin(adder_2_cout), .cout(adder_3_cout));
  Adder #(.width(1)) adder_4 (
    .a(multiplexer_4_out), .b(in_5[3]), .out(adder_1_out[3]), .cin(adder_3_cout));  // open: cout
  Multiplexer #(.width(4)) multiplexer_9 (.in0(adder_1_out), .in1(multiplexer_5_out), .out(out_7), .sel(in_6));
endmodule
