// Logisim project sameercomp.circ as structural Verilog: 1 circuit, main circuit main
module main (
  input  [1:0] in_1,
  input  in_2,
  input  in_3,
  input  [7:0] in_4,
  output [7:0] out_5
);

  wire clock_1_out, decoder_1_out1;
  wire [7:0] adder_1_out, multiplexer_1_out, ram_1_data, register_1_q, register_2_q;

  Clock clock_1 (.out(clock_1_out));
  Adder adder_1 (.a(register_2_q), .b(in_4), .out(adder_1_out), .cin(in_3));  // open: cout
  Register register_1 (.D(multiplexer_1_out), .en(in_1[1]), .Q(register_1_q), .clk(clock_1_out));  // open: clr
  RAM ram_1 (.addr(register_1_q), .data(ram_1_data), .clk(clock_1_out), .ld(decoder_1_out1), .clr(in_2));  // open: sel
  Register register_2 (.D(adder_1_out), .en(in_1[0]), .Q(register_2_q), .clk(clock_1_out));  // open: clr
  Register register_3 (.D(multiplexer_1_out), .en(in_1[0]), .Q(out_5), .clk(clock_1_out));  // open: clr
  Decoder #(.select(2)) decoder_1 (.out1(decoder_1_out1), .sel(in_1));  // open: out0, out2, out3
  Multiplexer #(.select(2), .width(8)) multiplexer_1 (
    .in1(ram_1_data), .in2(register_2_q), .out(multiplexer_1_out), .sel(in_1));  // open: in0, in3
endmodule
